# Fritzing sketch Lab3_Part_1 (saved by Fritzing 0.9.4)
breadboards: 1

parts:
  Part2 = Arduino Uno (Rev3) - ICSP
  LED1 = LEDs [package=led10mm]
  Photocell = S1133 Si Photodiode [package="8mm Ceramic [THT]"]
  10_K_Resistor = Resistor [tolerance=±5% resistance=220 package="0603 [SMD]"]
  10_K_Resistor1 = Resistor [tolerance=±5% resistance=220 package="0603 [SMD]"]

nets:
  N1: Part2.A0, Photocell.cathode, 10_K_Resistor.Pin_0
  N2: Part2.5V, Photocell.anode
  N3: Part2.GND, LED1.C, 10_K_Resistor.Pin_1
  N4: Part2.D3_PWM, 10_K_Resistor1.Pin_0
  N5: LED1.A, 10_K_Resistor1.Pin_1
