# Fritzing sketch Lab3_Part_2 (saved by Fritzing 0.9.4)
breadboards: 1

parts:
  Part2 = Arduino Uno (Rev3) - ICSP
  LED1 = LEDs [package=led10mm]
  Photocell = S1133 Si Photodiode [package="8mm Ceramic [THT]"]
  10_K_Resistor = Resistor [tolerance=±5% resistance=220 package="0603 [SMD]"]
  10_K_Resistor1 = Resistor [tolerance=±5% resistance=220 package="0603 [SMD]"]
  HC-SR04_Sensor_1 = HC-SR04 Ultrasonic Distance Sensor
  10_K_Resistor2 = Resistor [tolerance=±5% resistance=220 package="0603 [SMD]"]

nets:
  N1: Part2.A0, Photocell.cathode, 10_K_Resistor.Pin_0
  5V: Part2.5V, Photocell.anode, HC-SR04_Sensor_1.VCC
  N2: Part2.GND, 10_K_Resistor.Pin_1, HC-SR04_Sensor_1.ECHO
  N3: Part2.D12/MISO, HC-SR04_Sensor_1.GND
  N4: Part2.D13/SCK, HC-SR04_Sensor_1.TRIG
  N5: Part2.D3_PWM, 10_K_Resistor1.Pin_0
  N6: Part2.D5_PWM, 10_K_Resistor2.Pin_0
  N7: Part2.D6_PWM, LED1.C
  N8: LED1.A, 10_K_Resistor1.Pin_1, 10_K_Resistor2.Pin_1

notes:
  Pin 5 controls the green pin on LED and pin 3 controls the red pin
