# Fritzing sketch Lab3_Part_3 (saved by Fritzing 0.9.4)
breadboards: 1

parts:
  Part1 = OLED Monochrome 128x64 1.3 inch [part_number=938]
  RE1 = Rotary Encoder [package=THT]
  Part3 = Arduino Uno (Rev3) - ICSP

nets:
  N1: Part1.MOSI_SDA, Part3.D11_PWM/MOSI
  N2: Part1.SCLK_SCK, Part3.D12/MISO
  N3: Part1.DC_SA0, Part3.D9_PWM
  N4: Part1.RESET, Part3.D10_PWM/SS
  N5: Part1.CS, Part3.D8
  VIN: Part1.VIN, Part3.5V
  GND: Part1.GND, Part3.GND
  N6: RE1.EncoderPinA, Part3.D3_PWM
  N7: RE1.EncoderPinC, Part3.D4
  N8: RE1.EncoderPinB, Part3.D2

notes:
  The part we used had one more pin on each side that was connected to ground

custom parts:
  OLED Monochrome 128x64 1.3 inch: These displays are small, only about 1.3" diagonal, but very readable due to the high contrast of an OLED display. This display is made of 128x64 individual white OLED pixels, each one is turned on or off by the controller chip. Because the display makes its own light, no backlight is required. This reduces the power required to run the OLED and is why the display has such high contrast; we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
